# Fritzing sketch wiring_diagram_m4_rc_fritz (saved by Fritzing 0.9.10b)
breadboards: 1

parts:
  M1 = roboclaw_2x45a
  Part1 = Adafruit Metro with Headers [part_number="Adafruit #2488"]

nets:
  N1: M1.S1-Sig, Part1.IO3
  N2: M1.S2-Sig, Part1.IO2
  N3: M1.S1-PWR, M1.S2-PWR, M1.S3-PWR, Part1.+5V
  N4: M1.EN1_-, M1.S1-GND, M1.S2-GND, Part1.GND

custom parts:
  roboclaw_2x45a: Roboclaw 2x45 motor driver.
  Adafruit Metro with Headers: We sure love the ATmega328 here at Adafruit, and we use them a lot for our own projects. The processor has plenty of GPIO, Analog inputs, hardware UART SPI and I2C, timers and PWM galore - just enough for most simple projects. When we need to go small, we use a Pro Trinket 3V or 5V, but when size isn't as much of a concern, and an USB-serial converter is required, we reach for an Adafruit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
